// Logisim project tt_test.circ as structural Verilog: 2 circuits, main circuit main
module main (
  input  RST,
  input  CLK,
  output A,
  output B,
  output C,
  output D,
  output E,
  output F,
  output G,
  output DP
);

  wire buffer_1_out, buffer_2_out, buffer_3_out, buffer_4_out, d_ff_1_q, d_ff_2_q, d_ff_3_q, d_ff_4_q,
       d_ff_5_qn;

  D_Flip_Flop d_ff_1 (.D(buffer_4_out), .clk(CLK), .Q(d_ff_1_q), .preset(RST));  // open: Qn, reset
  or or_1 (A, d_ff_2_q, d_ff_4_q);
  or or_2 (B, d_ff_1_q, d_ff_2_q, d_ff_3_q, d_ff_4_q);
  D_Flip_Flop d_ff_2 (.D(buffer_1_out), .clk(CLK), .Q(d_ff_2_q), .reset(RST));  // open: Qn, preset
  buf buffer_1 (buffer_1_out, d_ff_1_q);
  or or_3 (C, d_ff_1_q, d_ff_3_q, d_ff_4_q);
  or or_4 (D, d_ff_2_q, d_ff_4_q);
  or or_5 (E, d_ff_2_q, d_ff_4_q);
  or or_6 (F, d_ff_3_q, d_ff_4_q);
  D_Flip_Flop d_ff_3 (.D(buffer_2_out), .clk(CLK), .Q(d_ff_3_q), .reset(RST));  // open: Qn, preset
  buf buffer_2 (buffer_2_out, d_ff_2_q);
  or or_7 (G, d_ff_2_q, d_ff_3_q, d_ff_4_q);
  buf buffer_3 (buffer_3_out, d_ff_3_q);
  buf buffer_4 (buffer_4_out, d_ff_4_q);
  D_Flip_Flop d_ff_4 (.D(buffer_3_out), .clk(CLK), .Q(d_ff_4_q), .reset(RST));  // open: Qn, preset
  D_Flip_Flop d_ff_5 (.D(d_ff_5_qn), .clk(CLK), .Q(DP), .Qn(d_ff_5_qn), .reset(RST));  // open: preset
endmodule

module test (
);

  wire button_1_out, clock_1_out, main_1_a, main_1_b, main_1_c, main_1_d, main_1_dp, main_1_e, main_1_f,
       main_1_g;

  Button button_1 (.out(button_1_out));
  Clock clock_1 (.out(clock_1_out));
  main main_1 (
    .RST(button_1_out), .CLK(clock_1_out), .A(main_1_a), .B(main_1_b), .C(main_1_c), .D(main_1_d),
    .E(main_1_e), .F(main_1_f), .G(main_1_g), .DP(main_1_dp));
  _7_Segment_Display u_7_segment_display_1 (
    .g(main_1_g), .f(main_1_f), .a(main_1_a), .b(main_1_b), .e(main_1_e), .d(main_1_d), .c(main_1_c),
    .dp(main_1_dp));
endmodule
